# Fritzing sketch AFAmp23cm Design, Schematic (saved by Fritzing 0.9.3b)
circuit board: 8.46667cm x 5.64444cm
breadboards: 1

parts:
  R1 = Resistor [tolerance=±5% resistance=5.1k package=THT]
  R3 = Resistor [tolerance=±5% resistance=560 package=THT]
  C1 = Ceramic Capacitor [capacitance=220nF package="100 mil [THT, multilayer]"]
  C3 = Ceramic Capacitor [capacitance=1µF package="100 mil [THT, multilayer]"]
  R2 = Resistor [tolerance=±5% resistance=1k package=THT]
  Q1 = NPN-Transistor [package="TO92 [THT]"]
  R4 = Resistor [tolerance=±5% resistance=100 package=THT]
  C2 = Electrolytic Capacitor [capacitance=47µF package="100 mil [THT, electrolytic]"]
  TRS1 = Stereo Jack (TRS) 3.5mm [package="PG203J [THT]"]
  R5 = Resistor [tolerance=±5% resistance=5.1k package=THT]
  R6 = Resistor [tolerance=±5% resistance=560 package=THT]
  C4 = Ceramic Capacitor [capacitance=220nF package="100 mil [THT, multilayer]"]
  C5 = Ceramic Capacitor [capacitance=1µF package="100 mil [THT, multilayer]"]
  R7 = Resistor [tolerance=±5% resistance=1k package=THT]
  Q2 = NPN-Transistor [package="TO92 [THT]"]
  R8 = Resistor [tolerance=±5% resistance=100 package=THT]
  C6 = Electrolytic Capacitor [capacitance=47µF package="100 mil [THT, electrolytic]"]

nets:
  N1: R1.Pin_0, R3.Pin_1, R5.Pin_0, R6.Pin_1
  N2: R1.Pin_1, C1.1, R2.Pin_0, Q1.B
  N3: R3.Pin_0, C3.0, Q1.C
  N4: C1.0, TRS1.Ring, TRS1.Tip
  N5: C3.1, C4.0
  N6: R2.Pin_1, R4.Pin_1, C2.-, TRS1.Sleeve, R7.Pin_1, R8.Pin_1, C6.-
  N7: Q1.E, R4.Pin_0, C2.+
  N8: R5.Pin_1, C4.1, R7.Pin_0, Q2.B
  N9: R6.Pin_0, C5.0, Q2.C
  N10: Q2.E, R8.Pin_0, C6.+
